# Fritzing sketch Motor_a_Pasos (saved by Fritzing 0.9.3b)
breadboards: 1

parts:
  IC1 = L293D [package=THT]
  M1 = Stepper Motor - Bipolar
  Componente1 = Arduino Uno (Rev3)

nets:
  N1: IC1.Enable_1, IC1.+Vmotor, IC1.Enable_2, IC1.+V, Componente1.5V
  N2: IC1.In_1, Componente1.D8
  N3: IC1.Out_1_(_Controlled_by_Enable_1_), M1.A
  N4: IC1.0V, Componente1.GND
  N5: IC1.Out_2_(_Controlled_by_Enable_1_), M1.C
  N6: IC1.In_2, Componente1.D9_PWM
  N7: IC1.In_3, Componente1.D10_PWM/SS
  N8: IC1.Out_3_(_Controlled_by_Enable_2_), M1.B
  N9: IC1.Out_4_(_Controlled_by_Enable_2_), M1.D
  N10: IC1.In_4, Componente1.D11_PWM/MOSI
