# Fritzing sketch Servo (saved by Fritzing 0.9.3b)
circuit board: 6.88566cm x 5.36311cm
breadboards: 1

parts:
  J1 = Basic Servo
  Arduino2 = Arduino Uno (Rev3)
  R1 = Rotary Potentiometer (Small) [maximum_resistance=100kΩ package=THT]

nets:
  GND: J1.gnd, Arduino2.GND, R1.leg2
  VCC: J1.vcc, Arduino2.5V, R1.leg1
  N1: J1.pulse, Arduino2.D9_PWM
  N2: Arduino2.A2, R1.wiper
