# Fritzing sketch ModuloWiFi (saved by Fritzing 0.9.3b)
breadboards: 1

parts:
  Componente1 = Arduino Uno (Rev3)
  U2 = ESP8266 WiFi Module [part_number=ESP8266]

nets:
  N1: Componente1.D2, U2.TXD
  N2: Componente1.D3_PWM, U2.RXD
  3V3: Componente1.3V3, U2.VCC, U2.CH_PD
  GND: Componente1.GND, U2.GND

custom parts:
  ESP8266 WiFi Module: Generic WiFi Module based on the ESP8266 with onboard PCB antenna and UART communications
