# Fritzing sketch LCDPractice (saved by Fritzing 0.9.3b)
breadboards: 1

parts:
  Componente1 = Arduino Uno (Rev3)
  U1 = POT_SWITCH [package=pot_pth]
  U2 = LCD-16X2 [package=lcd-16x2]

nets:
  N1: Componente1.D8, U2.E
  N2: Componente1.D9_PWM, U2.DB4
  N3: Componente1.D10_PWM/SS, U2.DB5
  N4: Componente1.D11_PWM/MOSI, U2.DB6
  N5: Componente1.D12/MISO, U2.DB7
  N6: Componente1.D7, U2.RS
  5V: Componente1.5V, U1.G$1_A, U2.VDD, U2.A
  GND: Componente1.GND, U1.G$1_E, U2.VSS, U2.R_W, U2.K
  N7: U1.G$2_1, U2.VO
